# Fritzing sketch Project4 (saved by Fritzing 0.9.1b)
breadboards: 1

parts:
  PIR1 = PIR sensor
  LED1 = LED - 3mm [color="Red (633nm)" package="3 mm [THT]"]
  R1 = Resistor [tolerance=±5% resistance=220 package=THT]
  Raspberry_Pi1 = Raspberry Pi B+
  LED3 = LED - 3mm [color="Red (633nm)" package="3 mm [THT]"]
  R3 = Resistor [tolerance=±5% resistance=220 package=THT]
  LED4 = LED - 3mm [color="Red (633nm)" package="3 mm [THT]"]
  R4 = Resistor [tolerance=±5% resistance=220 package=THT]
  LED5 = LED - 3mm [color="Red (633nm)" package="3 mm [THT]"]
  R5 = Resistor [tolerance=±5% resistance=220 package=THT]
  LED6 = LED - 3mm [color="Red (633nm)" package="3 mm [THT]"]
  R6 = Resistor [tolerance=±5% resistance=220 package=THT]
  LED7 = LED - 3mm [color="Red (633nm)" package="3 mm [THT]"]
  R7 = Resistor [tolerance=±5% resistance=220 package=THT]
  J1 = Piezo Speaker
  S1 = Momentary Switch [package=ksa_sealed_tac_switch]

nets:
  VDD: PIR1.VDD, Raspberry_Pi1.5V
  N1: PIR1.SIG, Raspberry_Pi1.GPIO26
  GND: PIR1.GND, R1.Pin_1, Raspberry_Pi1.GND, R3.Pin_1, R4.Pin_1, R5.Pin_0, R6.Pin_0, J1.pin1, S1.3
  N2: LED1.cathode, R1.Pin_0
  N3: LED1.anode, Raspberry_Pi1.GPIO17
  N4: Raspberry_Pi1.GPIO27, LED3.anode
  N5: Raspberry_Pi1.GPIO22, LED4.anode
  N6: Raspberry_Pi1.GPIO10, LED5.anode
  N7: Raspberry_Pi1.GPIO9, LED6.anode
  N8: Raspberry_Pi1.GPIO11, LED7.anode
  N9: Raspberry_Pi1.GPIO13, S1.1
  N10: Raspberry_Pi1.GPIO19, J1.pin2
  N11: LED3.cathode, R3.Pin_0
  N12: LED4.cathode, R4.Pin_0
  N13: LED5.cathode, R5.Pin_1
  N14: LED6.cathode, R6.Pin_1
  N15: LED7.cathode, R7.Pin_1
